# Fritzing sketch iot (saved by Fritzing 0.9.3b)
breadboards: 1

parts:
  Part1 = RFID-RC522-v2
  LED1 = LED - 5mm [color="Green (555nm)" package="5 mm [THT]"]
  LED2 = LED - 5mm [color="Red (633nm)" package="5 mm [THT]"]
  R1 = Resistor [tolerance=±5% resistance=220 package=THT]
  U1 = ESP32S-HiLetgo [part_number=ESP32S-HiLetgo]
  R3 = Resistor [tolerance=±5% resistance=220 package=THT]

nets:
  N1: Part1.SDA, U1.GPIO21
  N2: Part1.SCK, U1.GPIO18
  N3: Part1.MOSI, U1.GPIO23
  N4: Part1.MISO, U1.GPIO19
  GND: Part1.GND, LED1.cathode, LED2.cathode, U1.GND
  N5: Part1.RST, U1.GPIO22
  N6: Part1.3.3V, U1.3.3
  N7: LED1.anode, R3.Pin_1
  N8: LED2.anode, R1.Pin_1
  N9: R1.Pin_0, U1.GPIO32
  N10: U1.GPIO12, R3.Pin_0

notes:
  3.3V
  RST
  GND
  SDA
  SCK
  MOSI
  MISO
  18
  19
  21
  22
  23
  12
  32

custom parts:
  RFID-RC522-v2: A simple China made RFID-RC522 Reader; do check the pin labels, as this is a MFRC522 based clone.
  ESP32S-HiLetgo: HiLetgo ESP-WROOM-32 ESP32 ESP-32S Development Board 2.4GHz Dual-Mode WiFi + Bluetooth Dual Cores Microcontroller The ESP32 integrated with Antenna switches, RF Balun, power amplifiers, low-noise amplifiers, filters, and management modules, and the entire solution occupies the least area of PCB. 2.4 GHz Wi-Fi plus Bluetooth dual-mode chip, with TSMC Ultra-low power consumption 40nm technology,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
